# Fritzing sketch artifact-counter (saved by Fritzing 0.9.2b)
circuit board: 10cm x 7.5cm
breadboards: 6

parts:
  U1 = atmega328 [package=dip]
  VCC1 = Battery block 9V
  C1 = Electrolytic Capacitor [capacitance=22µF package="0605 [SMD, electrolytic]"]
  C2 = Ceramic Capacitor [capacitance=10nF package="100 mil [THT, multilayer]"]
  LED1 = smd LED [color="Red (633nm)" package="0603 [SMD]"]
  R1 = Resistor [tolerance=±5% resistance=330 package="0603 [SMD]"]
  U3 = Voltage Regulator - 5V [package="DPak [SMD]"]
  R2 = Resistor [tolerance=±5% resistance=10k package="0603 [SMD]"]
  XTAL1 = Crystal [frequency="16 Mhz" package=THT]
  C6 = Ceramic Capacitor [capacitance=22pF package="1206 [SMD, multilayer]"]
  C7 = Ceramic Capacitor [capacitance=22pF package="1206 [SMD, multilayer]"]
  U4 = 74HC595 [package="DIP16 [THT]"]
  U5 = 74HC595 [package="DIP16 [THT]"]
  U6 = 74HC595 [package="DIP16 [THT]"]
  R3 = Resistor [tolerance=±5% resistance=330 package="0603 [SMD]"]
  R4 = Resistor [tolerance=±5% resistance=330 package="0603 [SMD]"]
  R5 = Resistor [tolerance=±5% resistance=330 package="0603 [SMD]"]
  R6 = Resistor [tolerance=±5% resistance=330 package="0603 [SMD]"]
  R7 = Resistor [tolerance=±5% resistance=330 package="0603 [SMD]"]
  R8 = Resistor [tolerance=±5% resistance=330 package="0603 [SMD]"]
  R9 = Resistor [tolerance=±5% resistance=330 package="0603 [SMD]"]
  R10 = Resistor [tolerance=±5% resistance=330 package="0603 [SMD]"]  # not connected
  R11 = Resistor [tolerance=±5% resistance=330 package="0603 [SMD]"]  # not connected
  R12 = Resistor [tolerance=±5% resistance=330 package="0603 [SMD]"]  # not connected
  R13 = Resistor [tolerance=±5% resistance=330 package="0603 [SMD]"]  # not connected
  R14 = Resistor [tolerance=±5% resistance=330 package="0603 [SMD]"]  # not connected
  R15 = Resistor [tolerance=±5% resistance=330 package="0603 [SMD]"]  # not connected
  R16 = Resistor [tolerance=±5% resistance=330 package="0603 [SMD]"]  # not connected
  R17 = Resistor [tolerance=±5% resistance=330 package="0603 [SMD]"]
  R18 = Resistor [tolerance=±5% resistance=330 package="0603 [SMD]"]
  R19 = Resistor [tolerance=±5% resistance=330 package="0603 [SMD]"]
  R20 = Resistor [tolerance=±5% resistance=330 package="0603 [SMD]"]
  R21 = Resistor [tolerance=±5% resistance=330 package="0603 [SMD]"]
  R22 = Resistor [tolerance=±5% resistance=330 package="0603 [SMD]"]
  R23 = Resistor [tolerance=±5% resistance=330 package="0603 [SMD]"]
  S4 = Momentary Switch [package=ksa_sealed_tac_switch]  # not connected
  S5 = Momentary Switch [package=ksa_sealed_tac_switch]
  S6 = Momentary Switch [package=ksa_sealed_tac_switch]  # not connected
  S7 = Momentary Switch [package=ksa_sealed_tac_switch]
  S8 = Momentary Switch [package=ksa_sealed_tac_switch]  # not connected
  S9 = Momentary Switch [package=ksa_sealed_tac_switch]  # not connected
  S10 = Momentary Switch [package=ksa_sealed_tac_switch]  # not connected
  U7 = SWITCH_SPDT [package=kps-1290]
  S12 = Momentary Switch [package=ksa_sealed_tac_switch]
  S11 = Momentary Switch [package=ksa_sealed_tac_switch]  # not connected
  7_Segment5 = 7 Segment Display
  7_Segment4 = 7 Segment Display
  7_Segment6 = 7 Segment Display
  LED6 = smd LED [color="Red (633nm)" package="0603 [SMD]"]
  LED7 = smd LED [color="Red (633nm)" package="0603 [SMD]"]
  LED8 = smd LED [color="Red (633nm)" package="0603 [SMD]"]
  LED9 = smd LED [color="Red (633nm)" package="0603 [SMD]"]

nets (from the breadboard view):
  N1: U1.RESET, R2.Pin_1
  N2: U1.D3_(PWM), S12.4
  N3: U1.VCC, C2.0, LED1.cathode, U3.output_voltage, R2.Pin_0, U5.MR
  N4: U1.GND#7, VCC1.-, C1.-, C2.1, R1.Pin_0, U3.GND, C6.1, C7.1
  N5: U1.XLAT1, XTAL1.pin_0, C6.0
  N6: U1.XLAT2, XTAL1.pin_1, C7.0
  N7: U1.D11_(PWM), U4.DS
  N8: U1.D12, U4.ST_CP, U5.ST_CP, U6.ST_CP
  N9: U1.D13, U4.SH_CP, U5.SH_CP, U6.SH_CP
  VCC: U1.AVCC, U1.AREF, U4.MR, U4.VCC, U5.VCC, U6.MR, U6.VCC
  GND: U1.GND#21, U4.GND, U4.OE, U5.GND, U5.OE, U6.GND, U6.OE, S7.4, U7.P, 7_Segment5.common_cathode, 7_Segment4.common_anode, 7_Segment6.common_cathode
  N10: U1.A0, LED6.anode
  N11: U1.A1, LED7.anode
  N12: U1.A2, LED8.anode
  N13: U1.A3, LED9.anode
  N14: U1.A4, U7.S
  N15: U1.A5, U7.O
  N16: VCC1.+, C1.+, U3.input_voltage
  N17: LED1.anode, R1.Pin_1
  N18: U4.Q1, R9.Pin_0
  N19: U4.Q2, R8.Pin_0
  N20: U4.Q3, R7.Pin_0
  N21: U4.Q4, R6.Pin_0
  N22: U4.Q5, R5.Pin_0
  N23: U4.Q6, R4.Pin_0
  N24: U4.Q7', U5.DS
  N25: U4.Q0, R3.Pin_0
  N26: U5.Q7', U6.DS
  N27: U6.Q1, R22.Pin_0
  N28: U6.Q2, R18.Pin_0
  N29: U6.Q3, R21.Pin_0
  N30: U6.Q4, R19.Pin_0
  N31: U6.Q5, R17.Pin_0
  N32: U6.Q6, R20.Pin_0
  N33: U6.Q0, R23.Pin_0
  N34: R3.Pin_1, 7_Segment6.Segment_A
  N35: R5.Pin_1, 7_Segment6.Segment_F
  N36: R6.Pin_1, 7_Segment6.Segment_E
  N37: R7.Pin_1, 7_Segment6.Segment_D
  N38: R8.Pin_1, 7_Segment6.Segment_C
  N39: R9.Pin_1, 7_Segment6.Segment_B
  N40: R17.Pin_1, 7_Segment5.Segment_F
  N41: R18.Pin_1, 7_Segment5.Segment_C
  N42: R19.Pin_1, 7_Segment5.Segment_E
  N43: R20.Pin_1, 7_Segment5.Segment_G
  N44: R21.Pin_1, 7_Segment5.Segment_D
  N45: R22.Pin_1, 7_Segment5.Segment_B
  N46: R23.Pin_1, 7_Segment5.Segment_A
  N47: S5.3, S5.4
  N48: S7.1, S7.2
  N49: LED6.cathode, LED7.cathode, LED8.cathode, LED9.cathode
